# Fritzing sketch UmiTempBluetooth (saved by Fritzing 0.9.2b)
breadboards: 1

parts:
  DHT2 = DHT11 Humitidy and Temperature Sensor
  T1 = TMP36 Temperature Sensor [package="TO92 [THT]"]
  Componente1 = Bluetooth HC-05 Macho
  Componente2 = Arduino Uno (Rev3)
  R1 = Resistor [tolerance=±5% resistance=10k package=THT]

nets:
  VDD: DHT2.VDD, T1.+Vs, Componente1.VCC, Componente2.5V, R1.Pin_0
  N1: DHT2.DATA, Componente2.D7, R1.Pin_1
  GND: DHT2.GND, T1.GND, Componente1.GND, Componente2.GND
  N2: T1.Vout, Componente2.A0
  N3: Componente1.TXD, Componente2.D10_PWM/SS
  N4: Componente1.RXD, Componente2.D11_PWM/MOSI

custom parts:
  DHT11 Humitidy and Temperature Sensor: DHT11 Humidity and Temperature Sensor
